# Fritzing sketch moisture-1 (saved by Fritzing 0.9.3b)
circuit board: 8.46667cm x 5.64444cm
breadboards: 1

parts:
  VCC1 = Battery
  U1 = atmega328 [package=dip]
  Q1 = NPN-Transistor [package="TO92 [THT]"]
  R2 = Resistor [tolerance=±5% resistance=1k package="2512 [SMD]"]
  U2 = V_REG_LD1117VXX [part_number=LD1117V33 package=78xxl]
  C1 = Electrolytic Capacitor [capacitance=100nF package="100 mil [THT, electrolytic]"]
  C2 = Electrolytic Capacitor [capacitance=10µF package="100 mil [THT, electrolytic]"]
  Part1 = NRF24L01+ Breakout Board
  Part3 = Soil Moisture Sensor

nets:
  GND: VCC1.-, U1.GND, Q1.C, U2.GND, C1.-, C2.-, Part1.GND
  N1: VCC1.+, U2.IN, C1.+
  N2: U1.D4, R2.Pin_1
  VCC: U1.VCC, U1.AVCC, U1.AREF, U2.OUT, C2.+, Part1.VCC, Part3.VCC
  N3: U1.D9_(PWM), Part1.CS
  N4: U1.D10_(PWM), Part1.CE
  N5: U1.D11_(PWM), Part1.MOSI
  N6: U1.D12, Part1.MISO
  N7: U1.D13, Part1.SCK
  N8: U1.A0, Part3.SIG
  N9: Q1.E, Part3.GND
  N10: Q1.B, R2.Pin_0
